# Fritzing sketch esp32thing (saved by Fritzing 1.0.1rc)
circuit board: 9.6773cm x 7.17313cm

parts:
  Bauteil3 = GY-VL53L0XV2 Laser Ranger Module
  LevelShifter1 = I2C level shifter bidirectional
  LevelShifter2 = I2C level shifter bidirectional
  USB = USB connector [package=THT]
  SparkFun_ESP32_Thing = SparkFun ESP32 Thing [part_number=DEV-13907]

nets:
  VCC: Bauteil3.VCC, LevelShifter1.LV, LevelShifter2.LV, SparkFun_ESP32_Thing.3.3V
  GND: Bauteil3.GND, LevelShifter1.GND, LevelShifter2.GND, SparkFun_ESP32_Thing.GND
  N1: LevelShifter1.LV4, SparkFun_ESP32_Thing.16
  N2: LevelShifter1.LV3, SparkFun_ESP32_Thing.21
  N3: LevelShifter1.LV2, SparkFun_ESP32_Thing.U0RXD
  N4: LevelShifter1.LV1, SparkFun_ESP32_Thing.U0TXD
  N5: LevelShifter1.HV, LevelShifter2.HV, SparkFun_ESP32_Thing.VUSB-RAW, SparkFun_ESP32_Thing.V_BATT
  N6: LevelShifter1.HV4, USB.5V
  N7: LevelShifter2.LV4, SparkFun_ESP32_Thing.25
  N8: LevelShifter2.LV3, SparkFun_ESP32_Thing.26
  N9: LevelShifter2.LV2, SparkFun_ESP32_Thing.27
  N10: LevelShifter2.LV1, SparkFun_ESP32_Thing.14
  N11: LevelShifter2.HV4, USB.d+

notes:
  GPIO25 --> LS --> Auger Isolater (output)
  GPIO26 --> LS --> Reset (output)
  GPIO27 --> LS --> Auger Isolator (input)
  GPIO14 --> LS --> Timer LED (output) (changed from GPIO19 due to layout)
  GPIO21(RX1) --> LS --> RX Display Board
  GPIO01(TX0) --> LS --> TuyaMCU(RX)
  GPIO03(RX0) --> LS --> TuyaMCU(TX)
  GPIO16(RX2) --> LS --> TX Display Board

custom parts:
  GY-VL53L0XV2 Laser Ranger Module: The GY-VL53L0XV2 is based on the VL53L0X from ST Microelectronics, a time-of-flight ranging system integrated into a compact module.
  SparkFun ESP32 Thing: The SparkFun ESP32 Thing is a comprehensive development platform for Espressif’s ESP32, their super-charged version of the popular ESP8266. Like the 8266, the ESP32 is a WiFi-compatible microcontroller, but to that it adds support for Bluetooth low-energy (i.e BLE, BT4.0, Bluetooth Smart), and nearly 30 I/O pins. The ESP32’s power and versatility will make it the foundation of IoT and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
